# Fritzing sketch Wiring Layout (saved by Fritzing 0.9.4)
breadboards: 1

parts:
  Raspberry_Pi1 = Raspberry Pi B+
  Disable_sunrise_mode = Tactile Switch Buttons - 12mm Square [package=tactile-pth-12mm]
  Start_/_Stop_sunset_mode = Tactile Switch Buttons - 12mm Square [package=tactile-pth-12mm]
  Switch_nightlight = Tactile Switch Buttons - 12mm Square [package=tactile-pth-12mm]
  neopixel1 = Neopixel Ring 16
  part = POT [part_number=Potentiometer package=alps_pot]
  U2 = LCD-16X2 [package=lcd-16x2]

nets:
  GND: Raspberry_Pi1.GND, Disable_sunrise_mode.1, Disable_sunrise_mode.3, Start_/_Stop_sunset_mode.1, Start_/_Stop_sunset_mode.3, Switch_nightlight.2, Switch_nightlight.4, neopixel1.GND, part.E, U2.VSS, U2.R_W, U2.K
  N1: Raspberry_Pi1.GPIO27, U2.DB7
  N2: Raspberry_Pi1.GPIO22, U2.DB6
  N3: Raspberry_Pi1.GPIO19, U2.E
  5V: Raspberry_Pi1.GPIO26, Raspberry_Pi1.5V, neopixel1.VCC, part.A, U2.VDD, U2.VO, U2.A
  N4: Raspberry_Pi1.GPIO16, Switch_nightlight.1, Switch_nightlight.3
  N5: Raspberry_Pi1.GPIO12, Disable_sunrise_mode.4
  N6: Raspberry_Pi1.GPIO25, U2.DB4
  N7: Raspberry_Pi1.GPIO24, U2.DB5
  N8: Raspberry_Pi1.GPIO23, Start_/_Stop_sunset_mode.2, Start_/_Stop_sunset_mode.4
  N9: Raspberry_Pi1.GPIO18, neopixel1.IN

custom parts:
  Tactile Switch Buttons - 12mm Square: Medium-sized clicky momentary switches are standard input "buttons" on electronic projects. These work best in a PCB but can be used on a solderless breadboard as shown in this tutorial. The pins are normally open (disconnected) and when the button is pressed they are momentarily closed. They come in a pack of 10, they're pretty handy so you'll want to keep them around. You can find an EAGLE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
  Neopixel Ring 16: Neopixel Ring x16
